// Logisim project cpu.circ as structural Verilog: 19 circuits, main circuit cpu
module cpu (
);

  wire and_1_out, CLK, CTL, eret, Fail, Go, hasIntr, IR1, IR2, IR3, lock_IF_ID, lock_PC, miss, not_1_out,
       npc_1_is_j, or_1_out, or_2_out, pause, RST, rst_ID_EX, W1, W2, W3;
  wire [1:0] syscall_1_out;
  wire [2:0] controller_1_mem, controller_1_pc_control, ex_mem_1_out_14, id_ex_1_out_19, id_ex_1_out_25;
  wire [3:0] bubble_1_redirect, r_data_1_out_5;
  wire [4:0] controller_1_instruction, controller_1_ra, controller_1_rb, decoder_1_shamt, id_ex_1_out_17;
  wire [5:0] decoder_1_funct, decoder_1_op;
  wire [6:0] ex_mem_1_out_12, mem_wb_1_out_11;
  wire [7:0] controller_1_wb, ex_mem_1_out_13, id_ex_1_out_18, registerfile_1_p4;
  wire [9:0] divider_1_out_2;
  wire [10:0] id_ex_1_out_20;
  wire [10:4] controller_1_ex;
  wire [11:0] controller_1_will_r;
  wire [14:0] decoder_1_mix;
  wire [15:0] decoder_1_imm, \load_use次数 , \总周期数 , \插入气泡数 , \无条件分支指令数 , \有条件分支成功跳转 , \有条件分支指令数 ;
  wire [23:0] divider1_1_out_2;
  wire [25:0] decoder_1_label, id_ex_1_out_26;
  wire [31:0] alu_1_result, bht_1_npc, ex_mem_1_out_11, ex_mem_1_out_15, ex_mem_1_out_16, EX_PC,
       extender_1_out_4, extender_1_out_5, id_ex_1_out_16, id_ex_1_out_21, id_ex_1_out_22, id_ex_1_out_23,
       id_ex_1_out_24, ID_PC, if_id_1_out_7, if_id_1_out_8, IF_PC, interrupt_1_pc_out, MEM_PC,
       mem_wb_1_out_10, mem_wb_1_out_13, mem_wb_1_out_14, mips_ram_1_p8, multiplexer_1_out,
       multiplexer_2_out, multiplexer_3_out, multiplexer_4_out, multiplexer_5_out, npc_1_new_pc, npc_1_pc4,
       npc_1_will_go, PC_q, r_data_1_out_4, registerfile_1_p7, registerfile_1_p8, rom_1_data, SyscallOut,
       WB_PC;

  // Probe on npc_1_new_pc
  Button \u_总复位  (.out(RST));
  Button _1 (.out(IR1));
  Button _2 (.out(IR2));
  Button _3 (.out(IR3));
  Clock clock_1 (.out(CLK));
  interrupt interrupt_1 (
    .intr_btn1(IR1), .intr_LED1(W1), .PC_out(interrupt_1_pc_out), .intr_btn2(IR2), .intr_LED2(W2),
    .intr_btn3(IR3), .intr_LED3(W3), .eret(eret), .PC(npc_1_new_pc), .PC_EX(id_ex_1_out_16),
    .has_intr(hasIntr), .if_j(Fail), .PC_ID(if_id_1_out_7), .PC_IF(npc_1_pc4));
  Register #(.width(32)) PC (.D(bht_1_npc), .en(and_1_out), .Q(PC_q), .clk(CLK), .clr(RST));
  and and_1 (and_1_out, CTL, lock_PC);
  Button \u_继续运行  (.out(Go));
  LED led_1 (.in(W1));
  LED led_2 (.in(W2));
  LED led_3 (.in(W3));
  // Probe on IF_PC[11:0]
  SumPeriod sumperiod_1 (.in_1(CTL), .in_2(CLK), .out_4(\总周期数 ), .in_3(RST));
  NPC npc_1 (
    .PC_input(PC_q), .new_PC(npc_1_new_pc), .label(id_ex_1_out_26), .IMM(id_ex_1_out_24),
    .RF1(multiplexer_3_out), .pc_control(id_ex_1_out_25), .PC4(npc_1_pc4), .RF2(multiplexer_2_out),
    .rst(RST), .clk(CLK), .\成功Cnt (\有条件分支成功跳转 ), .halt(mem_wb_1_out_11[6]), .en(CTL), .oldPC(id_ex_1_out_16),
    .ALUout(alu_1_result), .fail(Fail), .pause(pause), .is_j(npc_1_is_j), .will_go(npc_1_will_go), .miss(miss));
  Hex_Digit_Display hex_digit_display_1 (.value(SyscallOut[31:28]));  // open: dp
  Hex_Digit_Display hex_digit_display_2 (.value(SyscallOut[23:20]));  // open: dp
  Hex_Digit_Display hex_digit_display_3 (.value(SyscallOut[27:24]));  // open: dp
  // Probe on ID_PC[11:0]
  Divider divider_1 (.in_1(PC_q), .out_2(divider_1_out_2));
  BHT bht_1 (
    .PC(PC_q), .new_entry(id_ex_1_out_16), .npc(bht_1_npc), .rst(RST), .if_success(Fail), .if_j(npc_1_is_j),
    .nPC_in(interrupt_1_pc_out), .clk(CLK), .miss(miss), .will_go(npc_1_will_go));
  Hex_Digit_Display hex_digit_display_4 (.value(SyscallOut[19:16]));  // open: dp
  Hex_Digit_Display hex_digit_display_5 (.value(SyscallOut[15:12]));  // open: dp
  Subtractor #(.width(32)) subtractor_1 (.a(npc_1_pc4), .b(32'h4), .out(IF_PC));  // open: bin, bout
  // Probe on id_ex_1_out_25
  Hex_Digit_Display hex_digit_display_6 (.value(SyscallOut[11:8]));  // open: dp
  Hex_Digit_Display hex_digit_display_7 (.value(SyscallOut[7:4]));  // open: dp
  // Probe on EX_PC[11:0]
  ROM #(.addrWidth(10), .dataWidth(32)) rom_1 (.addr(divider_1_out_2), .data(rom_1_data));  // open: sel
  or or_1 (or_1_out, RST, hasIntr, eret, miss);
  Hex_Digit_Display hex_digit_display_8 (.value(SyscallOut[3:0]));  // open: dp
  // Probe on MEM_PC[11:0]
  IF_ID if_id_1 (
    .in_1(npc_1_pc4), .in_2(rom_1_data), .\传输状态In (lock_IF_ID), .CLK(CLK), .out_7(if_id_1_out_7),
    .out_8(if_id_1_out_8), .\同步清零 (or_1_out), .pause(pause));  // open: 传输状态Out
  pipelineCnt pipelinecnt_1 (
    .load_use(rst_ID_EX), .load_use_cnt(\load_use次数 ), .fail(Fail), .CLK(CLK), .bubble_cnt(\插入气泡数 ), .RST(RST));
  Controller controller_1 (
    .op(decoder_1_op), .funct(decoder_1_funct), .pc_control(controller_1_pc_control), .clk(CLK), .rst(RST),
    .\有条件Cnt (\有条件分支指令数 ), .\无条件Cnt (\无条件分支指令数 ), .ex(controller_1_ex), .mem(controller_1_mem),
    .WB(controller_1_wb), .instruction(controller_1_instruction), .mix(decoder_1_mix),
    .will_r(controller_1_will_r), .ra(controller_1_ra), .rb(controller_1_rb));
  // Probe on \总周期数 
  // Probe on \无条件分支指令数 
  // Probe on \有条件分支成功跳转 
  // Probe on \load_use次数 
  // Probe on \插入气泡数 
  // Probe on WB_PC[11:0]
  Subtractor #(.width(32)) subtractor_2 (.a(if_id_1_out_7), .b(32'h4), .out(ID_PC));  // open: bin, bout
  Multiplexer #(.select(2), .width(32), .disabled(0), .enable("false")) multiplexer_1 (
    .in0(mem_wb_1_out_14), .in1(mem_wb_1_out_10), .in2(mem_wb_1_out_13), .out(multiplexer_1_out),
    .sel(registerfile_1_p4[6:5]));  // open: in3
  Decoder decoder_1 (
    .shamt(decoder_1_shamt), .op(decoder_1_op), .label(decoder_1_label), .instruction(if_id_1_out_8),
    .funct(decoder_1_funct), .IMM(decoder_1_imm), .MIX(decoder_1_mix));
  Bubble bubble_1 (
    .rst_ID_EX(rst_ID_EX), .lock_PC(lock_PC), .will_r(controller_1_will_r), .rst(RST),
    .WB_EX(id_ex_1_out_18), .WB_MEM(ex_mem_1_out_13), .lock_IF_ID(lock_IF_ID), .ctl(CTL),
    .ex_i(id_ex_1_out_17), .mem_i(ex_mem_1_out_12[4:0]), .redirect(bubble_1_redirect));
  // RegisterFile registerfile_1: pin names not known; wires that end beside it: multiplexer_1_out, CLK, registerfile_1_p4[7], registerfile_1_p4[4:0], controller_1_ra, controller_1_rb, registerfile_1_p7, registerfile_1_p8
  Extender extender_1 (
    .in_1(decoder_1_shamt), .out_4(extender_1_out_4), .out_5(extender_1_out_5), .in_3(decoder_1_imm),
    .in_2(controller_1_instruction));
  Cmp cmp_1 (.lhs(5'b01110), .res(eret), .rhs(controller_1_instruction));  // open: res_n
  ID_EX id_ex_1 (
    .WB(controller_1_wb), .MEM(controller_1_mem), .EX({controller_1_ex, bubble_1_redirect}),
    .A(registerfile_1_p7), .B(registerfile_1_p8), .shamt(extender_1_out_4), .IMM(extender_1_out_5),
    .CLK(CLK), .out_18(id_ex_1_out_18), .out_19(id_ex_1_out_19), .out_20(id_ex_1_out_20),
    .out_21(id_ex_1_out_21), .out_22(id_ex_1_out_22), .out_23(id_ex_1_out_23), .out_24(id_ex_1_out_24),
    .\同步清零 (or_2_out), .PC4(if_id_1_out_7), .out_16(id_ex_1_out_16), .instruction(controller_1_instruction),
    .out_17(id_ex_1_out_17), .PC_control(controller_1_pc_control), .out_25(id_ex_1_out_25),
    .Label(decoder_1_label), .out_26(id_ex_1_out_26), .\传输状态In (CTL), .pause(pause));  // open: 传输状态Out
  or or_2 (or_2_out, miss, hasIntr, rst_ID_EX);
  // Probe on id_ex_1_out_16
  Subtractor #(.width(32)) subtractor_3 (.a(id_ex_1_out_16), .b(32'h4), .out(EX_PC));  // open: bin, bout
  Multiplexer #(.select(2), .width(32), .disabled(0), .enable("false")) multiplexer_2 (
    .in0(id_ex_1_out_22), .in1(mem_wb_1_out_14), .in2(ex_mem_1_out_15), .in3(mem_wb_1_out_13),
    .out(multiplexer_2_out), .sel(id_ex_1_out_20[3:2]));
  Multiplexer #(.select(2), .width(32), .disabled(0), .enable("false")) multiplexer_3 (
    .in0(id_ex_1_out_21), .in1(mem_wb_1_out_14), .in2(ex_mem_1_out_15), .in3(mem_wb_1_out_13),
    .out(multiplexer_3_out), .sel(id_ex_1_out_20[1:0]));
  Syscall syscall_1 (
    .en(id_ex_1_out_20[10]), .cnt(SyscallOut), .clk(CLK), .rst(RST), .a0(multiplexer_2_out),
    .v0(multiplexer_3_out), .out(syscall_1_out), .i_pause(pause));
  Multiplexer #(.width(32), .disabled(0), .enable("false")) multiplexer_4 (
    .in0(multiplexer_3_out), .in1(id_ex_1_out_23), .out(multiplexer_4_out), .sel(id_ex_1_out_20[4]));
  Multiplexer #(.width(32), .disabled(0), .enable("false")) multiplexer_5 (
    .in0(multiplexer_2_out), .in1(id_ex_1_out_24), .out(multiplexer_5_out), .sel(id_ex_1_out_20[5]));
  ALU alu_1 (.AluOP(id_ex_1_out_20[9:6]), .X(multiplexer_4_out), .Result(alu_1_result), .Y(multiplexer_5_out));
  EX_MEM ex_mem_1 (
    .WB(id_ex_1_out_18), .MEM(id_ex_1_out_19), .ALUout(alu_1_result), .B(multiplexer_2_out), .CLK(CLK),
    .out_13(ex_mem_1_out_13), .out_14(ex_mem_1_out_14), .out_15(ex_mem_1_out_15), .out_16(ex_mem_1_out_16),
    .\同步清零 (RST), .PC4(id_ex_1_out_16), .out_11(ex_mem_1_out_11),
    .instruction({syscall_1_out, id_ex_1_out_17}), .out_12(ex_mem_1_out_12), .\传输状态In (CTL), .pause(pause));  // open: 传输状态Out
  Subtractor #(.width(32)) subtractor_4 (.a(ex_mem_1_out_11), .b(32'h4), .out(MEM_PC));  // open: bin, bout
  Divider1 divider1_1 (.in_1(ex_mem_1_out_15), .out_2(divider1_1_out_2));
  r_Data r_data_1 (
    .in_1(ex_mem_1_out_16), .out_4(r_data_1_out_4), .in_2(ex_mem_1_out_15[1:0]), .in_3(ex_mem_1_out_14[2]),
    .out_5(r_data_1_out_5));
  // MIPS_RAM mips_ram_1: pin names not known; wires that end beside it: divider1_1_out_2, r_data_1_out_4, ex_mem_1_out_14[1], r_data_1_out_5, CLK, ex_mem_1_out_14[0], RST, mips_ram_1_p8
  MEM_WB mem_wb_1 (
    .WB(ex_mem_1_out_13), .CLK(CLK), .out_12(registerfile_1_p4), .\同步清零 (RST), .ALUout(ex_mem_1_out_15),
    .out_14(mem_wb_1_out_14), .Data(mips_ram_1_p8), .out_13(mem_wb_1_out_13), .PC4(ex_mem_1_out_11),
    .out_10(mem_wb_1_out_10), .instruction(ex_mem_1_out_12), .out_11(mem_wb_1_out_11), .\传输状态In (CTL),
    .pause(pause));  // open: 传输状态Out
  Subtractor #(.width(32)) subtractor_5 (.a(mem_wb_1_out_10), .b(32'h4), .out(WB_PC));  // open: bin, bout
  not not_1 (not_1_out, pause);
  Register #(.width(1)) PC_2 (.D(mem_wb_1_out_11[5]), .en(not_1_out), .Q(pause), .clk(CLK), .clr(Go));

  // Notes on the sheet:
  //   中断源
  //   中断请求指示
  //   contents of rom_1 (hex, n*v repeats v):
  //   20110001 8000c05 20110001 20120002 20130003 8000c09 20110001 20120002 20130003 8000c0d 20110001
  //   20120002 20130003 8000c11 20110001 20120002 20130003 c000cf6 20100001 20110001 118fc0 112020
  //   20020022 c 118882 12200001 8000c15 112020 20020022 c 20110001 118880 112020 20020022 c 12200001
  //   8000c1f 20110001 118fc0 112020 20020022 c 1188c3 112020 20020022 c 118903 112020 20020022 c 118903
  //   112020 20020022 c 118903 112020 20020022 c 118903 112020 20020022 c 118903 112020 20020022 c 118903
  //   112020 20020022 c 118903 112020 20020022 c 20100001 109fc0 139fc3 8021 2012000c 24160003 26100001
  //   3210000f 20080008 20090001 139900 2709825 132020 20020022 c 1094022 1500fff9 22100001 2018000f
  //   2188024 108700 20080008 20090001 139902 2709825 132021 20020022 c 1094022 1500fff9 108702 2c9b022
  //   12c00001 8000c50 4020 1084027 84400 3508ffff 82021 20020022 c 2010ffff 20110000 ae300000 22100001
  //   22310004 ae300000 22100001 22310004 ae300000 22100001 22310004 ae300000 22100001 22310004 ae300000
  //   22100001 22310004 ae300000 22100001 22310004 ae300000 22100001 22310004 ae300000 22100001 22310004
  //   ae300000 22100001 22310004 ae300000 22100001 22310004 ae300000 22100001 22310004 ae300000 22100001
  //   22310004 ae300000 22100001 22310004 ae300000 22100001 22310004 ae300000 22100001 22310004 ae300000
  //   22100001 22310004 22100001 8020 2011003c 8e130000 8e340000 274402a 11000002 ae330000 ae140000
  //   2231fffc 1611fff8 102020 20020022 c 22100004 2011003c 1611fff2 20020032 c 20090000 200b0020 20110000
  //   20120001 a1310000 112020 20020022 c 2328820 21290001 216bffff 1560fff8 200b0008 20090000 8d310000
  //   112020 20020022 c 21290004 216bffff 1560fff9 20020032 c 2008ffff 20117777 112020 20020022 c 200b0010
  //   3a31ffff 112020 20020022 c 216bffff 1560fffa 20020032 c 2011fff1 112020 20020022 c 22310001 620fffb
  //   20020032 c 20080001 20090003 20110876 118d00 112020 20020022 c 200b0008 1118806 1318806 112020
  //   20020022 c 216bffff 1560fff9 2002000a c 20100000 22100001 102020 20020022 c 22100002 102020 20020022
  //   c 22100003 102020 20020022 c 22100004 102020 20020022 c 22100005 102020 20020022 c 22100006 102020
  //   20020022 c 22100007 102020 20020022 c 22100008 102020 20020022 20020022 c 3e00008
  //   数码管输出
  //   alu
  //   pc4
  //   load
endmodule

module Controller (
  input  [5:0] op,
  input  [5:0] funct,
  input  clk,
  input  rst,
  input  [14:0] mix,
  output [2:0] pc_control,
  output [15:0] \有条件Cnt ,
  output [4:0] instruction,
  output [4:0] rb,
  output [4:0] ra,
  output [15:0] \无条件Cnt ,
  output [6:0] ex,
  output [2:0] mem,
  output [7:0] WB,
  output [11:0] will_r
);

  wire add, addi, addiu, adds, addu, \and , andi, ands, beq, bltz, bne, cmps, comparator_1_eq,
       comparator_17_eq, comparator_18_eq, comparator_19_eq, comparator_20_eq, comparator_21_eq,
       comparator_22_eq, comparator_23_eq, comparator_24_eq, comparator_25_eq, comparator_26_eq,
       comparator_27_eq, comparator_28_eq, comparator_29_eq, comparator_30_eq, eret, j, jal, jr, js, \nor ,
       \or , or_2_out, or_10_out, or_12_out, or_13_out, ori, ors, Ra_t, rlshifters, sll, slt, slti, sltu,
       sra, srl, srlv, sub, sw, tmpR, xori;
  wire [1:0] Rw;

  Comparator #(.width(6)) comparator_1 (.a(op), .b({6{1'b0}}), .eq(comparator_1_eq));  // open: gt, lt
  Comparator #(.width(6)) comparator_2 (.a(op), .b(6'b001000), .eq(addi));  // open: gt, lt
  Comparator #(.width(6)) comparator_3 (.a(op), .b(6'b001001), .eq(addiu));  // open: gt, lt
  Comparator #(.width(6)) comparator_4 (.a(op), .b(6'b001100), .eq(andi));  // open: gt, lt
  Comparator #(.width(6)) comparator_5 (.a(op), .b(6'b001101), .eq(ori));  // open: gt, lt
  Comparator #(.width(6)) comparator_6 (.a(op), .b(6'b001110), .eq(xori));  // open: gt, lt
  Comparator #(.width(6)) comparator_7 (.a(op), .b(6'b001010), .eq(slti));  // open: gt, lt
  Comparator #(.width(6)) comparator_8 (.a(op), .b(6'b100011), .eq(mem[0]));  // open: gt, lt
  Comparator #(.width(6)) comparator_9 (.a(op), .b(6'b101011), .eq(sw));  // open: gt, lt
  Comparator #(.width(6)) comparator_10 (.a(op), .b(6'b101000), .eq(mem[2]));  // open: gt, lt
  Comparator #(.width(6)) comparator_11 (.a(op), .b(6'b000100), .eq(beq));  // open: gt, lt
  Comparator #(.width(6)) comparator_12 (.a(op), .b(6'b000101), .eq(bne));  // open: gt, lt
  Comparator #(.width(6)) comparator_13 (.a(op), .b(6'b000001), .eq(bltz));  // open: gt, lt
  Comparator #(.width(6)) comparator_14 (.a(op), .b(6'b000010), .eq(j));  // open: gt, lt
  Comparator #(.width(6)) comparator_15 (.a(op), .b(6'b000011), .eq(jal));  // open: gt, lt
  Comparator #(.width(6)) comparator_16 (.a(op), .b(6'b010000), .eq(eret));  // open: gt, lt
  Comparator #(.width(6)) comparator_17 (.a(funct), .b(6'b100000), .eq(comparator_17_eq));  // open: gt, lt
  Comparator #(.width(6)) comparator_18 (.a(funct), .b(6'b100001), .eq(comparator_18_eq));  // open: gt, lt
  Comparator #(.width(6)) comparator_19 (.a(funct), .b(6'b100100), .eq(comparator_19_eq));  // open: gt, lt
  Comparator #(.width(6)) comparator_20 (.a(funct), .b(6'b100010), .eq(comparator_20_eq));  // open: gt, lt
  Comparator #(.width(6)) comparator_21 (.a(funct), .b(6'b100101), .eq(comparator_21_eq));  // open: gt, lt
  Comparator #(.width(6)) comparator_22 (.a(funct), .b(6'b100111), .eq(comparator_22_eq));  // open: gt, lt
  Comparator #(.width(6)) comparator_23 (.a(funct), .b(6'b000110), .eq(comparator_23_eq));  // open: gt, lt
  Comparator #(.width(6)) comparator_24 (.a(funct), .b(6'b101010), .eq(comparator_24_eq));  // open: gt, lt
  Comparator #(.width(6)) comparator_25 (.a(funct), .b(6'b101011), .eq(comparator_25_eq));  // open: gt, lt
  Comparator #(.width(6)) comparator_26 (.a(funct), .b({6{1'b0}}), .eq(comparator_26_eq));  // open: gt, lt
  Comparator #(.width(6)) comparator_27 (.a(funct), .b(6'b000011), .eq(comparator_27_eq));  // open: gt, lt
  Comparator #(.width(6)) comparator_28 (.a(funct), .b(6'b000010), .eq(comparator_28_eq));  // open: gt, lt
  Comparator #(.width(6)) comparator_29 (.a(funct), .b(6'b001000), .eq(comparator_29_eq));  // open: gt, lt
  Comparator #(.width(6)) comparator_30 (.a(funct), .b(6'b001100), .eq(comparator_30_eq));  // open: gt, lt
  and and_1 (add, comparator_1_eq, comparator_17_eq);
  and and_2 (addu, comparator_1_eq, comparator_18_eq);
  and and_3 (\and , comparator_1_eq, comparator_19_eq);
  and and_4 (sub, comparator_1_eq, comparator_20_eq);
  and and_5 (\or , comparator_1_eq, comparator_21_eq);
  and and_6 (\nor , comparator_1_eq, comparator_22_eq);
  and and_7 (srlv, comparator_1_eq, comparator_23_eq);
  and and_8 (slt, comparator_1_eq, comparator_24_eq);
  and and_9 (sltu, comparator_1_eq, comparator_25_eq);
  and and_10 (sll, comparator_1_eq, comparator_26_eq);
  and and_11 (sra, comparator_1_eq, comparator_27_eq);
  and and_12 (srl, comparator_1_eq, comparator_28_eq);
  and and_13 (jr, comparator_1_eq, comparator_29_eq);
  and and_14 (ex[6], comparator_1_eq, comparator_30_eq);
  // Probe on WB[4:0]
  Priority_Encoder #(.select(5)) priority_encoder_1 (
    .in0(addi), .in1(addiu), .in2(andi), .in3(ori), .in4(xori), .in5(slti), .in6(mem[0]), .in7(sw),
    .in8(mem[2]), .in9(beq), .in10(bne), .in11(bltz), .in12(j), .in13(jal), .in14(eret), .in15(add),
    .in16(addu), .in17(\and ), .in18(sub), .in19(\or ), .in20(\nor ), .in21(srlv), .in22(slt), .in23(sltu),
    .in24(sll), .in25(sra), .in26(srl), .in27(jr), .in28(ex[6]), .in29(1'b0), .in30(1'b0), .in31(1'b0),
    .out(instruction));  // open: gs, en_out, en_in
  or or_1 (ex[0], sll, sra, srl);
  or or_2 (or_2_out, addi, addiu, andi, ori, xori, slti, mem[0], sw, mem[2]);
  or or_3 (cmps, slti, bltz, slt);
  or or_4 (ors, \or , ori);
  or or_5 (ands, \and , andi);
  or or_6 (rlshifters, srlv, srl);
  Priority_Encoder #(.select(1)) priority_encoder_2 (
    .in0(1'b1), .in1(or_2_out), .out(ex[1]));  // open: gs, en_out, en_in
  or or_7 (adds, mem[0], add, addi, mem[2], addu, addiu, sw);
  Priority_Encoder #(.select(4)) priority_encoder_3 (
    .in0(1'b1), .in1(sra), .in2(rlshifters), .in3(1'b0), .in4(1'b0), .in5(adds), .in6(sub), .in7(ands),
    .in8(ors), .in9(xori), .in10(\nor ), .in11(cmps), .in12(sltu), .in13(1'b0), .in14(1'b0), .in15(1'b0),
    .out(ex[5:2]));  // open: gs, en_out, en_in
  // Probe on Rw
  Multiplexer #(.select(2), .width(5), .disabled(0), .enable("false")) multiplexer_1 (
    .in0(mix[4:0]), .in1(mix[9:5]), .in2({5{1'b1}}), .out(WB[4:0]), .sel(Rw));  // open: in3
  Multiplexer #(.width(5), .disabled(0), .enable("false")) multiplexer_2 (
    .in0(mix[9:5]), .in1(5'b00100), .out(rb), .sel(Ra_t));
  Multiplexer #(.width(5), .disabled(0), .enable("false")) multiplexer_3 (
    .in0(mix[14:10]), .in1(5'b00010), .out(ra), .sel(Ra_t));
  or or_8 (mem[1], sw, mem[2]);
  Priority_Encoder #(.select(1)) priority_encoder_4 (.in0(1'b1), .in1(ex[6]), .out(Ra_t));  // open: gs, en_out, en_in
  or or_9 (tmpR, addi, addiu, andi, ori, xori, slti, mem[0]);
  Priority_Encoder #(.select(2)) priority_encoder_5 (
    .in0(1'b1), .in1(jal), .in2(mem[0]), .in3(1'b0), .out(WB[6:5]));  // open: gs, en_out, en_in
  nor nor_1 (WB[7], sw, mem[2], beq, bne, bltz, j, jr, ex[6]);
  Priority_Encoder #(.select(2)) priority_encoder_6 (
    .in0(1'b1), .in1(tmpR), .in2(jal), .in3(1'b0), .out(Rw));  // open: gs, en_out, en_in
  or or_10 (or_10_out, jr, tmpR);
  // Probe on will_r[1:0]
  Priority_Encoder #(.select(2)) priority_encoder_7 (
    .in0(1'b1), .in1(or_10_out), .in2(js), .in3(1'b0), .out(will_r[1:0]));  // open: gs, en_out, en_in
  or or_11 (js, j, jal);
  Priority_Encoder priority_encoder_8 (
    .in0(1'b1), .in1(beq), .in2(bne), .in3(bltz), .in4(js), .in5(jr), .in6(1'b0), .in7(1'b0), .out(pc_control));  // open: en_in, gs, en_out
  Counter #(.width(16), .max('hffff)) counter_1 (
    .count(or_12_out), .Q(\有条件Cnt ), .clk(clk), .clr(rst));  // open: load, D, carry
  or or_12 (or_12_out, bltz, bne, beq);
  Counter #(.width(16), .max('hffff)) counter_2 (
    .count(or_13_out), .Q(\无条件Cnt ), .clk(clk), .clr(rst));  // open: load, D, carry
  or or_13 (or_13_out, j, jal, jr);

  assign will_r[11:2] = {rb, ra};

  // Other names for the same wires on the sheet: CPC[2:0] = pc_control; CA = ex[0]; CB = ex[1]; ALUop[3:0] = ex[5:2];
  //   SysC1 = ex[6]; syscall = ex[6]; ld = mem[0]; lw = mem[0]; str = mem[1]; sb = mem[2]; rt[4:0] = mix[9:5];
  //   rs[4:0] = mix[14:10]; Rb_t = Ra_t; RWR[4:0] = WB[4:0]; Din[1:0] = WB[6:5]; We = WB[7];
  //   will_r_t[1:0] = will_r[1:0]; 无条件[15:0] = \无条件Cnt ; 有条件[15:0] = \有条件Cnt 
endmodule

module NPC (
  input  [31:0] IMM,
  input  [31:0] PC_input,
  input  [31:0] oldPC,
  input  halt,
  input  [31:0] RF1,
  input  [2:0] pc_control,
  input  [31:0] ALUout,
  input  pause,
  input  clk,
  input  rst,
  input  miss,
  input  [25:0] label,
  input  [31:0] RF2,
  output [31:0] new_PC,
  output [31:0] will_go,
  output en,
  output [31:0] PC4,
  output fail,
  output [15:0] \成功Cnt ,
  output is_j
);

  wire and_2_out, and_3_out, and_4_out, comparator_1_eq, comparator_2_eq, comparator_3_eq, comparator_4_eq,
       comparator_5_eq, decoder_1_out1, decoder_1_out2, decoder_1_out3, decoder_1_out4, decoder_1_out5,
       not_1_out, or_2_out;
  wire [31:0] and_1_out, bit_extender_1_out, Cbeq, Cbltz, Cbne, multiplexer_5_out, PC4offset, PCLabel,
       shifter_1_out;

  Shifter #(.width(32)) shifter_1 (.in(IMM), .\dist (5'b00010), .out(shifter_1_out));
  Adder #(.width(32)) adder_1 (.a(PC_input), .b(32'h4), .out(PC4));  // open: cin, cout
  assign and_1_out = PC_input & 32'hf0000000;  // AND_Gate and_1, 32 bits wide
  assign bit_extender_1_out = {{4{1'b0}}, {label, 2'b00}};  // Bit_Extender bit_extender_1
  nor nor_1 (en, halt, pause);
  Adder #(.width(32)) adder_2 (.a(shifter_1_out), .b(oldPC), .out(PC4offset));  // open: cin, cout
  assign PCLabel = and_1_out | bit_extender_1_out;  // OR_Gate or_1, 32 bits wide
  Comparator #(.width(32)) comparator_1 (.a(RF1), .b(RF2), .eq(comparator_1_eq));  // open: gt, lt
  Multiplexer #(.width(32), .disabled(0), .enable("false")) multiplexer_1 (
    .in0(PC4), .in1(PC4offset), .out(Cbeq), .sel(comparator_1_eq));
  // Probe on Cbeq
  // Probe on PC4offset
  Multiplexer #(.width(32), .disabled(0), .enable("false")) multiplexer_2 (
    .in0(PC4offset), .in1(PC4), .out(Cbne), .sel(comparator_1_eq));
  Comparator #(.width(3)) comparator_2 (.a(pc_control), .b(3'b001), .eq(comparator_2_eq));  // open: gt, lt
  Comparator #(.width(3)) comparator_3 (.a(pc_control), .b(3'b010), .eq(comparator_3_eq));  // open: gt, lt
  not not_1 (not_1_out, comparator_1_eq);
  Comparator #(.width(3)) comparator_4 (.a(pc_control), .b(3'b011), .eq(comparator_4_eq));  // open: gt, lt
  Comparator #(.width(32)) comparator_5 (.a(ALUout), .b(32'h1), .eq(comparator_5_eq));  // open: gt, lt
  Multiplexer #(.width(32), .disabled(0), .enable("false")) multiplexer_3 (
    .in0(PC4), .in1(PC4offset), .out(Cbltz), .sel(comparator_5_eq));
  // Probe on Cbne
  Decoder_part #(.select(3), .enable("false")) decoder_1 (
    .out1(decoder_1_out1), .out2(decoder_1_out2), .out3(decoder_1_out3), .out4(decoder_1_out4),
    .out5(decoder_1_out5), .sel(pc_control));  // open: out0, out6, out7
  and and_2 (and_2_out, comparator_2_eq, comparator_1_eq);
  and and_3 (and_3_out, comparator_3_eq, not_1_out);
  and and_4 (and_4_out, comparator_4_eq, comparator_5_eq);
  Counter #(.width(16), .max('hffff)) counter_1 (
    .count(or_2_out), .Q(\成功Cnt ), .clk(clk), .clr(rst));  // open: load, D, carry
  or or_2 (or_2_out, and_2_out, and_3_out, and_4_out);
  or or_3 (is_j, decoder_1_out1, decoder_1_out2, decoder_1_out3, decoder_1_out4, decoder_1_out5);
  or or_4 (fail, decoder_1_out4, decoder_1_out5, or_2_out);
  Multiplexer #(.select(3), .width(32), .disabled(0), .enable("false")) multiplexer_4 (
    .in0(PC4), .in1(PC4offset), .in2(PC4offset), .in3(PC4offset), .in4(PCLabel), .in5(RF1), .in6({32{1'b0}}),
    .in7({32{1'b0}}), .out(will_go), .sel(pc_control));
  Multiplexer #(.select(3), .width(32), .disabled(0), .enable("false")) multiplexer_5 (
    .in0(PC4), .in1(Cbeq), .in2(Cbne), .in3(Cbltz), .in4(PCLabel), .in5(RF1), .in6({32{1'b0}}),
    .in7({32{1'b0}}), .out(multiplexer_5_out), .sel(pc_control));
  Multiplexer #(.width(32), .disabled(0), .enable("false")) multiplexer_6 (
    .in0(PC4), .in1(multiplexer_5_out), .out(new_PC), .sel(miss));

  // Other names for the same wires on the sheet: CNPC[2:0] = pc_control; Input[31:0] = PC_input; oldPC4[31:0] = oldPC;
  //   Output[31:0] = new_PC; success[15:0] = \成功Cnt 
endmodule

module Divider (
  input  [31:0] in_1,
  output [9:0] out_2
);


  assign out_2 = in_1[11:2];

  // Other names for the same wires on the sheet: Input[31:0] = in_1; Output[9:0] = in_1[11:2]
endmodule

module Divider1 (
  input  [31:0] in_1,
  output [23:0] out_2
);


  assign out_2 = in_1[25:2];

  // Other names for the same wires on the sheet: Input[31:0] = in_1; Output[23:0] = in_1[25:2]
endmodule

module Decoder (
  input  [31:0] instruction,
  output [4:0] shamt,
  output [5:0] op,
  output [25:0] label,
  output [14:0] MIX,
  output [5:0] funct,
  output [15:0] IMM
);


  assign funct = instruction[5:0];
  assign IMM = instruction[15:0];
  assign label = instruction[25:0];
  assign MIX = instruction[25:11];
  assign op = instruction[31:26];
  assign shamt = instruction[10:6];

  // Other names for the same wires on the sheet: Input[31:0] = instruction; s[4:0] = instruction[10:6];
  //   rd[4:0] = instruction[15:11]; rt[4:0] = instruction[20:16]; rs[4:0] = instruction[25:21]
endmodule

module Extender (
  input  [4:0] in_1,
  input  [4:0] in_2,
  input  [15:0] in_3,
  output [31:0] out_4,
  output [31:0] out_5
);

  wire cmp_1_res, cmp_2_res, cmp_3_res, or_1_out;
  wire [31:0] bit_extender_2_out, bit_extender_3_out;

  assign out_4 = {{27{in_1[4]}}, in_1};  // Bit_Extender bit_extender_1
  assign bit_extender_2_out = {{16{in_3[15]}}, in_3};  // Bit_Extender bit_extender_2
  assign bit_extender_3_out = {{16{1'b0}}, in_3};  // Bit_Extender bit_extender_3
  Cmp cmp_1 (.lhs(in_2), .res(cmp_1_res), .rhs(5'b00010));  // open: res_n
  Cmp cmp_2 (.lhs(in_2), .res(cmp_2_res), .rhs(5'b00011));  // open: res_n
  Cmp cmp_3 (.lhs(in_2), .res(cmp_3_res), .rhs(5'b00100));  // open: res_n
  Multiplexer #(.width(32), .disabled(0), .enable("false")) multiplexer_1 (
    .in0(bit_extender_2_out), .in1(bit_extender_3_out), .out(out_5), .sel(or_1_out));
  or or_1 (or_1_out, cmp_1_res, cmp_2_res, cmp_3_res);

  // Other names for the same wires on the sheet: eIMM[31:0] = out_5; es[31:0] = out_4; IMM[15:0] = in_3;
  //   instruction[4:0] = in_2; s[4:0] = in_1
endmodule

module SumPeriod (
  input  in_1,
  input  in_2,
  input  in_3,
  output [15:0] out_4
);

  Counter #(.width(16), .max('hffff)) counter_1 (
    .count(in_1), .Q(out_4), .clk(in_2), .clr(in_3));  // open: load, D, carry

  // Other names for the same wires on the sheet: CLK = in_2; cnt[15:0] = out_4; enable = in_1; RST = in_3
endmodule

module Syscall (
  input  en,
  input  clk,
  input  rst,
  input  [31:0] a0,
  input  [31:0] v0,
  input  i_pause,
  output [31:0] cnt,
  output [1:0] out
);

  wire and_1_out, and_2_out, comparator_1_eq, comparator_2_eq;

  Register #(.width(32)) register_1 (.D(a0), .en(and_1_out), .Q(cnt), .clk(clk), .clr(rst));
  and and_1 (and_1_out, en, ~i_pause);  // AND_Gate
  Comparator #(.width(32), .mode("unsigned")) comparator_1 (.a(v0), .b(32'h22), .eq(comparator_1_eq));  // open: gt, lt
  Comparator #(.width(32), .mode("unsigned")) comparator_2 (.a(v0), .b(32'h32), .eq(comparator_2_eq));  // open: gt, lt
  and and_2 (and_2_out, ~comparator_1_eq, en);  // AND_Gate
  and and_3 (out[0], comparator_2_eq, en);
  and and_4 (out[1], and_2_out, ~out[0]);  // AND_Gate

  // Other names for the same wires on the sheet: enable = en; pause = out[0]; halt = out[1]; Output[31:0] = cnt
endmodule

module IF_ID (
  input  [31:0] in_1,
  input  [31:0] in_2,
  input  \传输状态In ,
  input  pause,
  input  CLK,
  input  \同步清零 ,
  output [31:0] out_7,
  output [31:0] out_8,
  output \传输状态Out 
);

  wire and_1_out, multiplexer_3_out;
  wire [31:0] multiplexer_1_out, multiplexer_2_out;

  and and_1 (and_1_out, \传输状态In , ~pause);  // AND_Gate
  Multiplexer #(.width(32), .enable("false")) multiplexer_1 (
    .in0(in_1), .in1({32{1'b0}}), .out(multiplexer_1_out), .sel(\同步清零 ));
  Multiplexer #(.width(32), .enable("false")) multiplexer_2 (
    .in0(in_2), .in1({32{1'b0}}), .out(multiplexer_2_out), .sel(\同步清零 ));
  Multiplexer #(.enable("false")) multiplexer_3 (.in0(and_1_out), .in1(1'b0), .out(multiplexer_3_out), .sel(\同步清零 ));
  Register #(.width(32)) register_1 (.D(multiplexer_1_out), .en(and_1_out), .Q(out_7), .clk(CLK));  // open: clr
  Register #(.width(32)) register_2 (.D(multiplexer_2_out), .en(and_1_out), .Q(out_8), .clk(CLK));  // open: clr
  Register #(.width(1)) register_3 (.D(multiplexer_3_out), .en(and_1_out), .Q(\传输状态Out ), .clk(CLK));  // open: clr
endmodule

module ID_EX (
  input  [31:0] PC4,
  input  [4:0] instruction,
  input  [7:0] WB,
  input  [2:0] MEM,
  input  [10:0] EX,
  input  [31:0] A,
  input  [31:0] B,
  input  [31:0] shamt,
  input  [31:0] IMM,
  input  [2:0] PC_control,
  input  [25:0] Label,
  input  \传输状态In ,
  input  pause,
  input  CLK,
  input  \同步清零 ,
  output [31:0] out_16,
  output [4:0] out_17,
  output [7:0] out_18,
  output [2:0] out_19,
  output [10:0] out_20,
  output [31:0] out_21,
  output [31:0] out_22,
  output [31:0] out_23,
  output [31:0] out_24,
  output [2:0] out_25,
  output [25:0] out_26,
  output \传输状态Out 
);

  wire and_1_out, multiplexer_12_out;
  wire [2:0] multiplexer_4_out, multiplexer_10_out;
  wire [4:0] multiplexer_2_out;
  wire [7:0] multiplexer_3_out;
  wire [10:0] multiplexer_5_out;
  wire [25:0] multiplexer_11_out;
  wire [31:0] multiplexer_1_out, multiplexer_6_out, multiplexer_7_out, multiplexer_8_out, multiplexer_9_out;

  and and_1 (and_1_out, \传输状态In , ~pause);  // AND_Gate
  Multiplexer #(.width(32), .enable("false")) multiplexer_1 (
    .in0(PC4), .in1({32{1'b0}}), .out(multiplexer_1_out), .sel(\同步清零 ));
  Multiplexer #(.width(5), .enable("false")) multiplexer_2 (
    .in0(instruction), .in1({5{1'b0}}), .out(multiplexer_2_out), .sel(\同步清零 ));
  Multiplexer #(.width(8), .enable("false")) multiplexer_3 (
    .in0(WB), .in1({8{1'b0}}), .out(multiplexer_3_out), .sel(\同步清零 ));
  Multiplexer #(.width(3), .enable("false")) multiplexer_4 (
    .in0(MEM), .in1(3'b000), .out(multiplexer_4_out), .sel(\同步清零 ));
  Multiplexer #(.width(11), .enable("false")) multiplexer_5 (
    .in0(EX), .in1({11{1'b0}}), .out(multiplexer_5_out), .sel(\同步清零 ));
  Multiplexer #(.width(32), .enable("false")) multiplexer_6 (
    .in0(A), .in1({32{1'b0}}), .out(multiplexer_6_out), .sel(\同步清零 ));
  Multiplexer #(.width(32), .enable("false")) multiplexer_7 (
    .in0(B), .in1({32{1'b0}}), .out(multiplexer_7_out), .sel(\同步清零 ));
  Multiplexer #(.width(32), .enable("false")) multiplexer_8 (
    .in0(shamt), .in1({32{1'b0}}), .out(multiplexer_8_out), .sel(\同步清零 ));
  Multiplexer #(.width(32), .enable("false")) multiplexer_9 (
    .in0(IMM), .in1({32{1'b0}}), .out(multiplexer_9_out), .sel(\同步清零 ));
  Multiplexer #(.width(3), .enable("false")) multiplexer_10 (
    .in0(PC_control), .in1(3'b000), .out(multiplexer_10_out), .sel(\同步清零 ));
  Multiplexer #(.width(26), .enable("false")) multiplexer_11 (
    .in0(Label), .in1({26{1'b0}}), .out(multiplexer_11_out), .sel(\同步清零 ));
  Multiplexer #(.enable("false")) multiplexer_12 (.in0(and_1_out), .in1(1'b0), .out(multiplexer_12_out), .sel(\同步清零 ));
  Register #(.width(32)) register_1 (.D(multiplexer_1_out), .en(and_1_out), .Q(out_16), .clk(CLK));  // open: clr
  Register #(.width(5)) register_2 (.D(multiplexer_2_out), .en(and_1_out), .Q(out_17), .clk(CLK));  // open: clr
  Register register_3 (.D(multiplexer_3_out), .en(and_1_out), .Q(out_18), .clk(CLK));  // open: clr
  Register #(.width(3)) register_4 (.D(multiplexer_4_out), .en(and_1_out), .Q(out_19), .clk(CLK));  // open: clr
  Register #(.width(11)) register_5 (.D(multiplexer_5_out), .en(and_1_out), .Q(out_20), .clk(CLK));  // open: clr
  Register #(.width(32)) register_6 (.D(multiplexer_6_out), .en(and_1_out), .Q(out_21), .clk(CLK));  // open: clr
  Register #(.width(32)) register_7 (.D(multiplexer_7_out), .en(and_1_out), .Q(out_22), .clk(CLK));  // open: clr
  Register #(.width(32)) register_8 (.D(multiplexer_8_out), .en(and_1_out), .Q(out_23), .clk(CLK));  // open: clr
  Register #(.width(32)) register_9 (.D(multiplexer_9_out), .en(and_1_out), .Q(out_24), .clk(CLK));  // open: clr
  Register #(.width(3)) register_10 (.D(multiplexer_10_out), .en(and_1_out), .Q(out_25), .clk(CLK));  // open: clr
  Register #(.width(26)) register_11 (.D(multiplexer_11_out), .en(and_1_out), .Q(out_26), .clk(CLK));  // open: clr
  Register #(.width(1)) register_12 (.D(multiplexer_12_out), .en(and_1_out), .Q(\传输状态Out ), .clk(CLK));  // open: clr
endmodule

module EX_MEM (
  input  [31:0] PC4,
  input  [6:0] instruction,
  input  [7:0] WB,
  input  [2:0] MEM,
  input  [31:0] ALUout,
  input  [31:0] B,
  input  \传输状态In ,
  input  pause,
  input  CLK,
  input  \同步清零 ,
  output [31:0] out_11,
  output [6:0] out_12,
  output [7:0] out_13,
  output [2:0] out_14,
  output [31:0] out_15,
  output [31:0] out_16,
  output \传输状态Out 
);

  wire and_1_out, multiplexer_7_out;
  wire [2:0] multiplexer_4_out;
  wire [6:0] multiplexer_2_out;
  wire [7:0] multiplexer_3_out;
  wire [31:0] multiplexer_1_out, multiplexer_5_out, multiplexer_6_out;

  and and_1 (and_1_out, \传输状态In , ~pause);  // AND_Gate
  Multiplexer #(.width(32), .enable("false")) multiplexer_1 (
    .in0(PC4), .in1({32{1'b0}}), .out(multiplexer_1_out), .sel(\同步清零 ));
  Multiplexer #(.width(7), .enable("false")) multiplexer_2 (
    .in0(instruction), .in1({7{1'b0}}), .out(multiplexer_2_out), .sel(\同步清零 ));
  Multiplexer #(.width(8), .enable("false")) multiplexer_3 (
    .in0(WB), .in1({8{1'b0}}), .out(multiplexer_3_out), .sel(\同步清零 ));
  Multiplexer #(.width(3), .enable("false")) multiplexer_4 (
    .in0(MEM), .in1(3'b000), .out(multiplexer_4_out), .sel(\同步清零 ));
  Multiplexer #(.width(32), .enable("false")) multiplexer_5 (
    .in0(ALUout), .in1({32{1'b0}}), .out(multiplexer_5_out), .sel(\同步清零 ));
  Multiplexer #(.width(32), .enable("false")) multiplexer_6 (
    .in0(B), .in1({32{1'b0}}), .out(multiplexer_6_out), .sel(\同步清零 ));
  Multiplexer #(.enable("false")) multiplexer_7 (.in0(and_1_out), .in1(1'b0), .out(multiplexer_7_out), .sel(\同步清零 ));
  Register #(.width(32)) register_1 (.D(multiplexer_1_out), .en(and_1_out), .Q(out_11), .clk(CLK));  // open: clr
  Register #(.width(7)) register_2 (.D(multiplexer_2_out), .en(and_1_out), .Q(out_12), .clk(CLK));  // open: clr
  Register register_3 (.D(multiplexer_3_out), .en(and_1_out), .Q(out_13), .clk(CLK));  // open: clr
  Register #(.width(3)) register_4 (.D(multiplexer_4_out), .en(and_1_out), .Q(out_14), .clk(CLK));  // open: clr
  Register #(.width(32)) register_5 (.D(multiplexer_5_out), .en(and_1_out), .Q(out_15), .clk(CLK));  // open: clr
  Register #(.width(32)) register_6 (.D(multiplexer_6_out), .en(and_1_out), .Q(out_16), .clk(CLK));  // open: clr
  Register #(.width(1)) register_7 (.D(multiplexer_7_out), .en(and_1_out), .Q(\传输状态Out ), .clk(CLK));  // open: clr
endmodule

module MEM_WB (
  input  [31:0] PC4,
  input  [6:0] instruction,
  input  [7:0] WB,
  input  [31:0] Data,
  input  [31:0] ALUout,
  input  \传输状态In ,
  input  pause,
  input  CLK,
  input  \同步清零 ,
  output [31:0] out_10,
  output [6:0] out_11,
  output [7:0] out_12,
  output [31:0] out_13,
  output [31:0] out_14,
  output \传输状态Out 
);

  wire and_1_out, multiplexer_6_out;
  wire [6:0] multiplexer_2_out;
  wire [7:0] multiplexer_3_out;
  wire [31:0] multiplexer_1_out, multiplexer_4_out, multiplexer_5_out;

  and and_1 (and_1_out, \传输状态In , ~pause);  // AND_Gate
  Multiplexer #(.width(32), .enable("false")) multiplexer_1 (
    .in0(PC4), .in1({32{1'b0}}), .out(multiplexer_1_out), .sel(\同步清零 ));
  Multiplexer #(.width(7), .enable("false")) multiplexer_2 (
    .in0(instruction), .in1({7{1'b0}}), .out(multiplexer_2_out), .sel(\同步清零 ));
  Multiplexer #(.width(8), .enable("false")) multiplexer_3 (
    .in0(WB), .in1({8{1'b0}}), .out(multiplexer_3_out), .sel(\同步清零 ));
  Multiplexer #(.width(32), .enable("false")) multiplexer_4 (
    .in0(Data), .in1({32{1'b0}}), .out(multiplexer_4_out), .sel(\同步清零 ));
  Multiplexer #(.width(32), .enable("false")) multiplexer_5 (
    .in0(ALUout), .in1({32{1'b0}}), .out(multiplexer_5_out), .sel(\同步清零 ));
  Multiplexer #(.enable("false")) multiplexer_6 (.in0(and_1_out), .in1(1'b0), .out(multiplexer_6_out), .sel(\同步清零 ));
  Register #(.width(32)) register_1 (.D(multiplexer_1_out), .en(and_1_out), .Q(out_10), .clk(CLK));  // open: clr
  Register #(.width(7)) register_2 (.D(multiplexer_2_out), .en(and_1_out), .Q(out_11), .clk(CLK));  // open: clr
  Register register_3 (.D(multiplexer_3_out), .en(and_1_out), .Q(out_12), .clk(CLK));  // open: clr
  Register #(.width(32)) register_4 (.D(multiplexer_4_out), .en(and_1_out), .Q(out_13), .clk(CLK));  // open: clr
  Register #(.width(32)) register_5 (.D(multiplexer_5_out), .en(and_1_out), .Q(out_14), .clk(CLK));  // open: clr
  Register #(.width(1)) register_6 (.D(multiplexer_6_out), .en(and_1_out), .Q(\传输状态Out ), .clk(CLK));  // open: clr
endmodule

module Cmp (
  input  [4:0] lhs,
  input  [4:0] rhs,
  output res,
  output res_n
);

  Comparator #(.width(5), .mode("unsigned")) comparator_1 (.a(lhs), .b(rhs), .eq(res));  // open: gt, lt
  not not_1 (res_n, res);
endmodule

module Bubble (
  input  [11:0] will_r,
  input  rst,
  input  [7:0] WB_EX,
  input  [7:0] WB_MEM,
  input  ctl,
  input  [4:0] ex_i,
  input  [4:0] mem_i,
  output rst_ID_EX,
  output lock_PC,
  output lock_IF_ID,
  output [3:0] redirect
);

  wire and_1_out, and_2_out, and_3_out, and_6_out, and_7_out, and_12_out, and_13_out, and_14_out, and_15_out,
       and_16_out, and_17_out, and_19_out, both, cmp_1_res, cmp_2_res, cmp_3_res, cmp_4_res, cmp_5_res,
       cmp_6_res_n, cmp_7_res_n, cmp_8_res, cmp_9_res, crash, effect_rs, effect_rt, ex_rs, ex_rt, mem_rs,
       mem_rt, none, one, or_1_out, or_2_out, or_3_out;

  Decoder_part #(.select(2), .enable("false")) decoder_1 (
    .out0(both), .out1(one), .out2(none), .sel(will_r[1:0]));  // open: out3
  Cmp cmp_1 (.lhs(mem_i), .res(cmp_1_res), .rhs(5'b00110));  // open: res_n
  and and_1 (and_1_out, cmp_1_res, mem_rt, effect_rt);
  and and_2 (and_2_out, mem_rt, effect_rt);
  and and_3 (and_3_out, ex_rt, effect_rt);
  Cmp cmp_2 (.lhs(will_r[6:2]), .res(cmp_2_res), .rhs(WB_EX[4:0]));  // open: res_n
  Cmp cmp_3 (.lhs(will_r[11:7]), .res(cmp_3_res), .rhs(WB_EX[4:0]));  // open: res_n
  Cmp cmp_4 (.lhs(will_r[6:2]), .res(cmp_4_res), .rhs(WB_MEM[4:0]));  // open: res_n
  Cmp cmp_5 (.lhs(will_r[11:7]), .res(cmp_5_res), .rhs(WB_MEM[4:0]));  // open: res_n
  Priority_Encoder #(.select(2)) priority_encoder_1 (
    .in0(1'b1), .in1(and_2_out), .in2(and_3_out), .in3(and_1_out), .out(redirect[3:2]));  // open: gs, en_out, en_in
  Cmp cmp_6 (.lhs(will_r[6:2]), .rhs({5{1'b0}}), .res_n(cmp_6_res_n));  // open: res
  Cmp cmp_7 (.lhs(will_r[11:7]), .rhs({5{1'b0}}), .res_n(cmp_7_res_n));  // open: res
  and and_4 (ex_rt, cmp_3_res, WB_EX[7]);
  and and_5 (ex_rs, cmp_2_res, WB_EX[7]);
  and and_6 (and_6_out, cmp_6_res_n, cmp_2_res);
  and and_7 (and_7_out, cmp_3_res, cmp_7_res_n);
  and and_8 (mem_rs, WB_MEM[7], cmp_4_res);
  and and_9 (mem_rt, cmp_5_res, WB_MEM[7]);
  Cmp cmp_8 (.lhs(mem_i), .res(cmp_8_res), .rhs(5'b00110));  // open: res_n
  and and_10 (effect_rt, cmp_7_res_n, both);
  and and_11 (effect_rs, cmp_6_res_n, or_1_out);
  or or_1 (or_1_out, both, one);
  or or_2 (or_2_out, and_6_out, and_7_out);
  and and_12 (and_12_out, one, and_6_out);
  and and_13 (and_13_out, cmp_8_res, mem_rs, effect_rs);
  and and_14 (and_14_out, or_2_out, both);
  or or_3 (or_3_out, and_14_out, and_12_out);
  and and_15 (and_15_out, mem_rs, effect_rs);
  and and_16 (and_16_out, ex_rs, effect_rs);
  and and_17 (and_17_out, or_3_out, ~none);  // AND_Gate
  or or_4 (rst_ID_EX, rst, crash);
  not not_1 (lock_PC, crash);
  and and_18 (lock_IF_ID, ~crash, ctl);  // AND_Gate
  Priority_Encoder #(.select(2)) priority_encoder_2 (
    .in0(1'b1), .in1(and_15_out), .in2(and_16_out), .in3(and_13_out), .out(redirect[1:0]));  // open: gs, en_out, en_in
  Cmp cmp_9 (.lhs(ex_i), .res(cmp_9_res), .rhs(5'b00110));  // open: res_n
  and and_19 (and_19_out, WB_EX[7], and_17_out);
  and and_20 (crash, cmp_9_res, and_19_out);

  // Other names for the same wires on the sheet: ctl_A[1:0] = redirect[1:0]; ctl_B[1:0] = redirect[3:2];
  //   RWR_EX[4:0] = WB_EX[4:0]; Din_EX[1:0] = WB_EX[6:5]; We_EX = WB_EX[7]; RWR_MEM[4:0] = WB_MEM[4:0];
  //   Din_MEM[1:0] = WB_MEM[6:5]; We_MEM = WB_MEM[7]; will_r_t[1:0] = will_r[1:0]; rs[4:0] = will_r[6:2];
  //   rt[4:0] = will_r[11:7]
endmodule

module r_Data (
  input  [31:0] in_1,
  input  [1:0] in_2,
  input  in_3,
  output [31:0] out_4,
  output [3:0] out_5
);

  wire [3:0] multiplexer_3_out;
  wire [31:0] multiplexer_2_out, shifter_1_out, shifter_2_out, shifter_3_out;

  Shifter #(.width(32)) shifter_1 (.in(in_1), .\dist (5'b01000), .out(shifter_1_out));
  Shifter #(.width(32)) shifter_2 (.in(in_1), .\dist (5'b10000), .out(shifter_2_out));
  Shifter #(.width(32)) shifter_3 (.in(in_1), .\dist (5'b11000), .out(shifter_3_out));
  Multiplexer #(.width(32), .disabled(0), .enable("false")) multiplexer_1 (
    .in0(in_1), .in1(multiplexer_2_out), .out(out_4), .sel(in_3));
  Multiplexer #(.select(2), .width(32), .disabled(0), .enable("false")) multiplexer_2 (
    .in0(in_1), .in1(shifter_1_out), .in2(shifter_2_out), .in3(shifter_3_out), .out(multiplexer_2_out),
    .sel(in_2));
  Multiplexer #(.select(2), .width(4), .disabled(0), .enable("false")) multiplexer_3 (
    .in0(4'b0001), .in1(4'b0010), .in2(4'b0100), .in3(4'b1000), .out(multiplexer_3_out), .sel(in_2));
  Multiplexer #(.width(4), .disabled(0), .enable("false")) multiplexer_4 (
    .in0(4'b1111), .in1(multiplexer_3_out), .out(out_5), .sel(in_3));
endmodule

module pipelineCnt (
  input  load_use,
  input  fail,
  input  CLK,
  input  RST,
  output [15:0] load_use_cnt,
  output [15:0] bubble_cnt
);

  wire [15:0] counter_1_q, shifter_1_out;

  Counter #(.width(16), .max('hffff)) counter_1 (
    .count(fail), .Q(counter_1_q), .clk(CLK), .clr(RST));  // open: load, D, carry
  Counter #(.width(16), .max('hffff)) counter_2 (
    .count(load_use), .Q(load_use_cnt), .clk(CLK), .clr(RST));  // open: load, D, carry
  Shifter #(.width(16)) shifter_1 (.in(counter_1_q), .\dist (4'b0001), .out(shifter_1_out));
  Adder #(.width(16)) adder_1 (.a(shifter_1_out), .b(load_use_cnt), .out(bubble_cnt));  // open: cin, cout
endmodule

module interrupt (
  input  intr_btn1,
  input  intr_btn2,
  input  intr_btn3,
  input  eret,
  input  [31:0] PC_IF,
  input  [31:0] PC,
  input  [31:0] PC_EX,
  input  if_j,
  input  [31:0] PC_ID,
  output intr_LED1,
  output [31:0] PC_out,
  output has_intr,
  output intr_LED2,
  output intr_LED3
);

  wire and_1_out, and_2_out, and_3_out, clk, comparator_1_eq, comparator_2_eq, comparator_3_eq, d_ff_1_q,
       d_ff_2_q, d_ff_3_q, decoder_1_out1, decoder_1_out2, decoder_1_out3, has_intr_t, hasIntr, intr1, intr2,
       intr3, intr_en, nand_1_out, nand_2_out, nand_3_out, or_4_out, or_5_out, or_6_out, or_7_out, or_8_out;
  wire [1:0] choose, current;
  wire [31:0] multiplexer_2_out, multiplexer_3_out, multiplexer_5_out, multiplexer_7_out, PC_to_save, savePC,
       subtractor_1_out, subtractor_2_out, subtractor_3_out, subtractor_4_out, vector;

  Clock clock_1 (.out(clk));
  Decoder_part #(.select(2), .disabled(0), .enable("false")) decoder_1 (
    .out1(decoder_1_out1), .out2(decoder_1_out2), .out3(decoder_1_out3), .sel(current));  // open: out0
  nand nand_1 (nand_1_out, eret, decoder_1_out1);
  nand nand_2 (nand_2_out, eret, decoder_1_out2);
  nand nand_3 (nand_3_out, eret, decoder_1_out3);
  Priority_Encoder #(.select(2), .disabled(0)) priority_encoder_1 (
    .in0(1'b1), .in1(intr_LED1), .in2(intr_LED2), .in3(intr_LED3), .out(choose), .en_in(intr_en));  // open: gs, en_out
  Register #(.width(2)) register_1 (.D(choose), .en(has_intr), .Q(current), .clk(clk));  // open: clr
  D_Flip_Flop d_ff_1 (.clk(intr_btn1), .D(1'b1), .Q(d_ff_1_q), .reset(intr1));  // open: Qn, preset, en
  or or_1 (intr_LED1, intr1, d_ff_1_q);
  D_Flip_Flop d_ff_2 (.clk(intr_btn2), .D(1'b1), .Q(d_ff_2_q), .reset(intr2));  // open: Qn, preset, en
  or or_2 (intr_LED2, intr2, d_ff_2_q);
  D_Flip_Flop d_ff_3 (.clk(intr_btn3), .D(1'b1), .Q(d_ff_3_q), .reset(intr3));  // open: Qn, preset, en
  or or_3 (intr_LED3, intr3, d_ff_3_q);
  // Probe on PC
  or or_4 (or_4_out, d_ff_1_q, intr1);
  or or_5 (or_5_out, d_ff_2_q, intr2);
  or or_6 (or_6_out, d_ff_3_q, intr3);
  and and_1 (and_1_out, or_4_out, nand_1_out);
  and and_2 (and_2_out, or_5_out, nand_2_out);
  and and_3 (and_3_out, or_6_out, nand_3_out);
  D_Flip_Flop d_ff_4 (.clk(clk), .D(and_1_out), .Q(intr1));  // open: Qn, preset, en, reset
  D_Flip_Flop d_ff_5 (.clk(clk), .D(and_2_out), .Q(intr2));  // open: Qn, preset, en, reset
  D_Flip_Flop d_ff_6 (.clk(clk), .D(and_3_out), .Q(intr3));  // open: Qn, preset, en, reset
  Multiplexer #(.select(2), .width(32), .disabled(0), .enable("false")) multiplexer_1 (
    .in0({32{1'b0}}), .in1(32'h3118), .in2(32'h31c0), .in3(32'h3268), .out(vector), .sel(choose));
  // Probe on PC_out
  // Probe on PC_EX
  or or_7 (or_7_out, intr1, intr2, intr3);
  and and_4 (hasIntr, or_7_out, intr_en);
  Multiplexer #(.width(32), .disabled(0), .enable("false")) multiplexer_2 (
    .in0(PC_to_save), .in1(PC), .out(multiplexer_2_out), .sel(if_j));
  D_Flip_Flop d_ff_7 (.clk(clk), .D(if_j));  // open: Q, Qn, preset, en, reset
  D_Flip_Flop d_ff_8 (.clk(clk), .D(1'b1), .Qn(intr_en), .en(has_intr), .reset(eret));  // open: Q, preset
  Multiplexer #(.width(32), .disabled(0), .enable("false")) multiplexer_3 (
    .in0(PC), .in1(vector), .out(multiplexer_3_out), .sel(has_intr));
  and and_5 (has_intr_t, ~eret, hasIntr);  // AND_Gate
  Register #(.width(32)) register_2 (.D(multiplexer_2_out), .en(has_intr), .Q(savePC), .clk(clk));  // open: clr
  Multiplexer #(.width(32), .disabled(0), .enable("false")) multiplexer_4 (
    .in0(multiplexer_3_out), .in1(savePC), .out(PC_out), .sel(eret));
  // Probe on savePC
  or or_8 (or_8_out, intr_LED1, intr_LED2, intr_LED3);
  and and_6 (has_intr, or_8_out, intr_en);
  // Probe on PC_IF
  // Probe on PC_ID
  Subtractor #(.width(32)) subtractor_1 (.a(PC_IF), .b(32'h4), .out(subtractor_1_out));  // open: bin, bout
  // Probe on subtractor_2_out
  Subtractor #(.width(32)) subtractor_2 (.a(PC_ID), .b(32'h4), .out(subtractor_2_out));  // open: bin, bout
  Comparator #(.width(32)) comparator_1 (.a(PC_IF), .b({32{1'b0}}), .eq(comparator_1_eq));  // open: gt, lt
  Subtractor #(.width(32)) subtractor_3 (.a(PC_IF), .b(32'h4), .out(subtractor_3_out));  // open: bin, bout
  // Probe on subtractor_1_out
  Comparator #(.width(32)) comparator_2 (.a(PC_EX), .b({32{1'b0}}), .eq(comparator_2_eq));  // open: gt, lt
  Comparator #(.width(32)) comparator_3 (.a(PC_ID), .b({32{1'b0}}), .eq(comparator_3_eq));  // open: gt, lt
  Subtractor #(.width(32)) subtractor_4 (.a(PC_ID), .b(32'h4), .out(subtractor_4_out));  // open: bin, bout
  Multiplexer #(.width(32), .disabled(0), .enable("false")) multiplexer_5 (
    .in0(subtractor_3_out), .in1({32{1'b0}}), .out(multiplexer_5_out), .sel(comparator_1_eq));
  // Probe on PC_to_save
  Multiplexer #(.width(32), .disabled(0), .enable("false")) multiplexer_6 (
    .in0(PC_EX), .in1(multiplexer_7_out), .out(PC_to_save), .sel(comparator_2_eq));
  Multiplexer #(.width(32), .disabled(0), .enable("false")) multiplexer_7 (
    .in0(subtractor_4_out), .in1(multiplexer_5_out), .out(multiplexer_7_out), .sel(comparator_3_eq));

  // Other names for the same wires on the sheet: asyn_hasIntr = has_intr
endmodule

module BHT (
  input  [31:0] PC,
  input  [31:0] new_entry,
  input  [31:0] nPC_in,
  input  [31:0] will_go,
  input  clk,
  input  rst,
  input  if_success,
  input  if_j,
  output [31:0] npc,
  output miss
);

  wire and_2_out, and_4_out, and_8_out, and_12_out, and_13_out, and_22_out, asyn0, asyn1, asyn2, asyn3, b0,
       b1, b2, clr0, clr1, clr2, clr3, comparator_1_gt, comparator_2_gt, comparator_6_gt, comparator_7_gt,
       comparator_8_eq, comparator_9_eq, comparator_10_eq, comparator_11_eq, comparator_12_eq,
       comparator_13_eq, comparator_14_eq, comparator_15_eq, comparator_16_eq, comparator_17_eq,
       comparator_18_eq, comparator_19_eq, comparator_20_eq, comparator_21_eq, comparator_22_eq,
       comparator_23_eq, comparator_24_eq, comparator_25_eq, comparator_26_eq, comparator_27_eq,
       comparator_28_eq, comparator_29_eq, comparator_30_eq, comparator_31_eq, comparator_32_gt,
       decoder_1_out0, decoder_1_out1, decoder_1_out2, decoder_1_out3, f0, f1, f2, f3, find, hit, hit0, hit1,
       hit2, hit3, i0, i1, i2, i3, miss0, miss1, miss2, miss3, multiplexer_19_out, or_1_out, or_3_out,
       or_5_out, or_7_out, xor_1_out, xor_2_out, xor_3_out, xor_4_out;
  wire [1:0] FSM0, FSM1, FSM2, FSM3, h0, h1, h2, h3, multiplexer_8_out, multiplexer_10_out,
       multiplexer_11_out, multiplexer_13_out, multiplexer_15_out, n0, n1, n2, n3, pos,
       priority_encoder_1_out, priority_encoder_2_out, priority_encoder_4_out, priority_encoder_5_out,
       priority_encoder_6_out;
  wire [15:0] cnt0, cnt1, cnt2, cnt3, multiplexer_5_out, multiplexer_6_out;
  wire [31:0] a0, a1, a2, a3, instr_2_q, instr_3_q, instr_4_q, instr_q, multiplexer_16_out,
       multiplexer_17_out, multiplexer_18_out, multiplexer_20_out, multiplexer_21_out, PC4;

  or or_1 (or_1_out, f0, i0);
  and and_1 (i0, and_2_out, and_13_out);
  and and_2 (and_2_out, b0, b2);
  // Probe on PC
  Comparator #(.width(2), .mode("unsigned")) comparator_1 (.a(h0), .b(2'b01), .gt(comparator_1_gt));  // open: eq, lt
  Comparator #(.width(2), .mode("unsigned")) comparator_2 (.a(h2), .b(2'b01), .gt(comparator_2_gt));  // open: eq, lt
  Register #(.width(32)) instr (.D(new_entry), .en(i0), .Q(instr_q), .clk(clk), .clr(rst));
  Register #(.width(32)) address (.D(will_go), .en(i0), .Q(a0), .clk(clk), .clr(rst));
  // Probe on h0
  Register #(.width(2)) history (.D(n0), .en(or_1_out), .Q(h0), .clk(clk), .clr(rst));
  Counter #(.width(16), .max('hffff)) counter_1 (
    .count(1'b1), .Q(cnt0), .clk(clk), .clr(clr0));  // open: load, D, carry
  or or_2 (asyn0, hit0, i0);
  Comparator #(.width(16), .mode("unsigned")) comparator_3 (.a(cnt0), .b(cnt1), .gt(b0));  // open: eq, lt
  Comparator #(.width(16), .mode("unsigned")) comparator_4 (.a(cnt2), .b(cnt3), .gt(b1));  // open: eq, lt
  Multiplexer #(.width(2), .disabled(0), .enable("false")) multiplexer_1 (
    .in0(2'b00), .in1(2'b01), .out(FSM0), .sel(if_success));
  Multiplexer #(.width(2), .disabled(0), .enable("false")) multiplexer_2 (
    .in0(2'b00), .in1(2'b11), .out(FSM1), .sel(if_success));
  Multiplexer #(.width(2), .disabled(0), .enable("false")) multiplexer_3 (
    .in0(2'b00), .in1(2'b11), .out(FSM2), .sel(if_success));
  Multiplexer #(.width(2), .disabled(0), .enable("false")) multiplexer_4 (
    .in0(2'b10), .in1(2'b11), .out(FSM3), .sel(if_success));
  xor xor_1 (xor_1_out, if_success, comparator_1_gt);
  xor xor_2 (xor_2_out, if_success, comparator_2_gt);
  or or_3 (or_3_out, f1, i1);
  and and_3 (i1, and_4_out, and_13_out);
  and and_4 (and_4_out, ~b0, b2);  // AND_Gate
  Multiplexer #(.width(16), .disabled(0), .enable("false")) multiplexer_5 (
    .in0(cnt1), .in1(cnt0), .out(multiplexer_5_out), .sel(b0));
  Multiplexer #(.width(16), .disabled(0), .enable("false")) multiplexer_6 (
    .in0(cnt3), .in1(cnt2), .out(multiplexer_6_out), .sel(b1));
  and and_5 (miss0, if_j, xor_1_out);
  and and_6 (miss2, if_j, xor_2_out);
  Register #(.width(32)) instr_2 (.D(new_entry), .en(i1), .Q(instr_2_q), .clk(clk), .clr(rst));
  Register #(.width(32)) address_2 (.D(will_go), .en(i1), .Q(a1), .clk(clk), .clr(rst));
  // Probe on h1
  Register #(.width(2)) history_2 (.D(n1), .en(or_3_out), .Q(h1), .clk(clk), .clr(rst));
  Counter #(.width(16), .max('hffff)) counter_2 (
    .count(1'b1), .Q(cnt1), .clk(clk), .clr(clr1));  // open: load, D, carry
  or or_4 (asyn1, hit1, i1);
  Comparator #(.width(16), .mode("unsigned")) comparator_5 (
    .a(multiplexer_5_out), .b(multiplexer_6_out), .gt(b2));  // open: eq, lt
  Comparator #(.width(2), .mode("unsigned")) comparator_6 (.a(h1), .b(2'b01), .gt(comparator_6_gt));  // open: eq, lt
  Comparator #(.width(2), .mode("unsigned")) comparator_7 (.a(h3), .b(2'b01), .gt(comparator_7_gt));  // open: eq, lt
  or or_5 (or_5_out, f2, i2);
  and and_7 (i2, and_8_out, and_13_out);
  and and_8 (and_8_out, b1, ~b2);  // AND_Gate
  // Probe on new_entry
  Adder #(.width(32)) adder_1 (.a(PC), .b(32'h4), .out(PC4));  // open: cin, cout
  xor xor_3 (xor_3_out, if_success, comparator_6_gt);
  xor xor_4 (xor_4_out, if_success, comparator_7_gt);
  Register #(.width(32)) instr_3 (.D(new_entry), .en(i2), .Q(instr_3_q), .clk(clk), .clr(rst));
  Register #(.width(32)) address_3 (.D(will_go), .en(i2), .Q(a2), .clk(clk), .clr(rst));
  Register #(.width(2)) history_3 (.D(n2), .en(or_5_out), .Q(h2), .clk(clk), .clr(rst));
  Counter #(.width(16), .max('hffff)) counter_3 (
    .count(1'b1), .Q(cnt2), .clk(clk), .clr(clr2));  // open: load, D, carry
  or or_6 (asyn2, hit2, i2);
  Comparator #(.width(2)) comparator_8 (.a(h0), .b(2'b00), .eq(comparator_8_eq));  // open: gt, lt
  Comparator #(.width(2)) comparator_9 (.a(h0), .b(2'b01), .eq(comparator_9_eq));  // open: gt, lt
  Comparator #(.width(2)) comparator_10 (.a(h0), .b(2'b10), .eq(comparator_10_eq));  // open: gt, lt
  Comparator #(.width(2)) comparator_11 (.a(h0), .b(2'b11), .eq(comparator_11_eq));  // open: gt, lt
  Comparator #(.width(2)) comparator_12 (.a(h2), .b(2'b00), .eq(comparator_12_eq));  // open: gt, lt
  Comparator #(.width(2)) comparator_13 (.a(h2), .b(2'b01), .eq(comparator_13_eq));  // open: gt, lt
  Comparator #(.width(2)) comparator_14 (.a(h2), .b(2'b10), .eq(comparator_14_eq));  // open: gt, lt
  Comparator #(.width(2)) comparator_15 (.a(h2), .b(2'b11), .eq(comparator_15_eq));  // open: gt, lt
  and and_9 (miss1, if_j, xor_3_out);
  and and_10 (miss3, if_j, xor_4_out);
  // Probe on h2
  or or_7 (or_7_out, f3, i3);
  and and_11 (i3, and_12_out, and_13_out);
  and and_12 (and_12_out, ~b1, ~b2);  // AND_Gate
  Multiplexer #(.width(2), .disabled(0), .enable("false")) multiplexer_7 (
    .in0(multiplexer_8_out), .in1(2'b10), .out(n0), .sel(i0));
  Multiplexer #(.select(2), .width(2), .disabled(0), .enable("false")) multiplexer_8 (
    .in0(FSM0), .in1(FSM1), .in2(FSM2), .in3(FSM3), .out(multiplexer_8_out), .sel(priority_encoder_1_out));
  Priority_Encoder #(.select(2), .disabled(0)) priority_encoder_1 (
    .in0(comparator_8_eq), .in1(comparator_9_eq), .in2(comparator_10_eq), .in3(comparator_11_eq),
    .out(priority_encoder_1_out));  // open: gs, en_out, en_in
  Multiplexer #(.width(2), .disabled(0), .enable("false")) multiplexer_9 (
    .in0(multiplexer_10_out), .in1(2'b10), .out(n2), .sel(i2));
  Multiplexer #(.select(2), .width(2), .disabled(0), .enable("false")) multiplexer_10 (
    .in0(FSM0), .in1(FSM1), .in2(FSM2), .in3(FSM3), .out(multiplexer_10_out), .sel(priority_encoder_2_out));
  Priority_Encoder #(.select(2), .disabled(0)) priority_encoder_2 (
    .in0(comparator_12_eq), .in1(comparator_13_eq), .in2(comparator_14_eq), .in3(comparator_15_eq),
    .out(priority_encoder_2_out));  // open: gs, en_out, en_in
  Register #(.width(32)) instr_4 (.D(new_entry), .en(i3), .Q(instr_4_q), .clk(clk), .clr(rst));
  Register #(.width(32)) address_4 (.D(will_go), .en(i3), .Q(a3), .clk(clk), .clr(rst));
  Register #(.width(2)) history_4 (.D(n3), .en(or_7_out), .Q(h3), .clk(clk), .clr(rst));
  Counter #(.width(16), .max('hffff)) counter_4 (
    .count(1'b1), .Q(cnt3), .clk(clk), .clr(clr3));  // open: load, D, carry
  or or_8 (asyn3, hit3, i3);
  and and_13 (and_13_out, if_j, ~find);  // AND_Gate
  // Probe on nPC_in
  Comparator #(.width(32)) comparator_16 (.a(new_entry), .b(instr_q), .eq(comparator_16_eq));  // open: gt, lt
  Comparator #(.width(32)) comparator_17 (.a(new_entry), .b(instr_2_q), .eq(comparator_17_eq));  // open: gt, lt
  Comparator #(.width(32)) comparator_18 (.a(new_entry), .b(instr_3_q), .eq(comparator_18_eq));  // open: gt, lt
  Comparator #(.width(32)) comparator_19 (.a(new_entry), .b(instr_4_q), .eq(comparator_19_eq));  // open: gt, lt
  Comparator #(.width(32)) comparator_20 (.a(PC4), .b(instr_q), .eq(comparator_20_eq));  // open: gt, lt
  Comparator #(.width(32)) comparator_21 (.a(PC4), .b(instr_2_q), .eq(comparator_21_eq));  // open: gt, lt
  Comparator #(.width(32)) comparator_22 (.a(PC4), .b(instr_3_q), .eq(comparator_22_eq));  // open: gt, lt
  Comparator #(.width(32)) comparator_23 (.a(PC4), .b(instr_4_q), .eq(comparator_23_eq));  // open: gt, lt
  and and_14 (hit0, decoder_1_out0, hit);
  and and_15 (hit1, decoder_1_out1, hit);
  // Probe on h3
  and and_16 (hit2, decoder_1_out2, hit);
  Comparator #(.width(2)) comparator_24 (.a(h1), .b(2'b00), .eq(comparator_24_eq));  // open: gt, lt
  Comparator #(.width(2)) comparator_25 (.a(h1), .b(2'b01), .eq(comparator_25_eq));  // open: gt, lt
  Comparator #(.width(2)) comparator_26 (.a(h1), .b(2'b10), .eq(comparator_26_eq));  // open: gt, lt
  Comparator #(.width(2)) comparator_27 (.a(h1), .b(2'b11), .eq(comparator_27_eq));  // open: gt, lt
  Comparator #(.width(2)) comparator_28 (.a(h3), .b(2'b00), .eq(comparator_28_eq));  // open: gt, lt
  Comparator #(.width(2)) comparator_29 (.a(h3), .b(2'b01), .eq(comparator_29_eq));  // open: gt, lt
  Comparator #(.width(2)) comparator_30 (.a(h3), .b(2'b10), .eq(comparator_30_eq));  // open: gt, lt
  Comparator #(.width(2)) comparator_31 (.a(h3), .b(2'b11), .eq(comparator_31_eq));  // open: gt, lt
  or or_9 (find, comparator_16_eq, comparator_19_eq, comparator_18_eq, comparator_17_eq);
  Priority_Encoder #(.select(2), .disabled(0)) priority_encoder_3 (
    .in0(comparator_16_eq), .in1(comparator_17_eq), .in2(comparator_18_eq), .in3(comparator_19_eq), .out(pos));  // open: gs, en_out, en_in
  or or_10 (hit, comparator_20_eq, comparator_23_eq, comparator_22_eq, comparator_21_eq);
  Priority_Encoder #(.select(2), .disabled(0)) priority_encoder_4 (
    .in0(comparator_20_eq), .in1(comparator_21_eq), .in2(comparator_22_eq), .in3(comparator_23_eq),
    .out(priority_encoder_4_out));  // open: gs, en_out, en_in
  and and_17 (hit3, decoder_1_out3, hit);
  Priority_Encoder #(.select(2), .disabled(0)) priority_encoder_5 (
    .in0(comparator_24_eq), .in1(comparator_25_eq), .in2(comparator_26_eq), .in3(comparator_27_eq),
    .out(priority_encoder_5_out));  // open: gs, en_out, en_in
  Priority_Encoder #(.select(2), .disabled(0)) priority_encoder_6 (
    .in0(comparator_28_eq), .in1(comparator_29_eq), .in2(comparator_30_eq), .in3(comparator_31_eq),
    .out(priority_encoder_6_out));  // open: gs, en_out, en_in
  Multiplexer #(.select(2), .width(2), .disabled(0)) multiplexer_11 (
    .in0(h0), .in1(h1), .in2(h2), .in3(h3), .out(multiplexer_11_out), .sel(priority_encoder_4_out), .en(hit));
  Decoder_part #(.select(2), .disabled(0)) decoder_1 (
    .out0(decoder_1_out0), .out1(decoder_1_out1), .out2(decoder_1_out2), .out3(decoder_1_out3),
    .sel(priority_encoder_4_out), .en(hit));
  D_Flip_Flop d_ff_1 (.clk(clk), .D(asyn0), .Q(clr0));  // open: Qn, preset, en, reset
  D_Flip_Flop d_ff_2 (.clk(clk), .D(asyn1), .Q(clr1));  // open: Qn, preset, en, reset
  D_Flip_Flop d_ff_3 (.clk(clk), .D(asyn2), .Q(clr2));  // open: Qn, preset, en, reset
  D_Flip_Flop d_ff_4 (.clk(clk), .D(asyn3), .Q(clr3));  // open: Qn, preset, en, reset
  Multiplexer #(.width(2), .disabled(0), .enable("false")) multiplexer_12 (
    .in0(multiplexer_13_out), .in1(2'b10), .out(n1), .sel(i1));
  Multiplexer #(.select(2), .width(2), .disabled(0), .enable("false")) multiplexer_13 (
    .in0(FSM0), .in1(FSM1), .in2(FSM2), .in3(FSM3), .out(multiplexer_13_out), .sel(priority_encoder_5_out));
  Multiplexer #(.width(2), .disabled(0), .enable("false")) multiplexer_14 (
    .in0(multiplexer_15_out), .in1(2'b10), .out(n3), .sel(i3));
  Multiplexer #(.select(2), .width(2), .disabled(0), .enable("false")) multiplexer_15 (
    .in0(FSM0), .in1(FSM1), .in2(FSM2), .in3(FSM3), .out(multiplexer_15_out), .sel(priority_encoder_6_out));
  // Probe on npc
  and and_18 (f0, if_j, comparator_16_eq);
  and and_19 (f1, if_j, comparator_17_eq);
  and and_20 (f2, if_j, comparator_18_eq);
  and and_21 (f3, if_j, comparator_19_eq);
  Multiplexer #(.select(2), .width(32), .disabled(0)) multiplexer_16 (
    .in0(a0), .in1(a1), .in2(a2), .in3(a3), .out(multiplexer_16_out), .sel(priority_encoder_4_out), .en(hit));
  Comparator #(.width(2), .mode("unsigned")) comparator_32 (
    .a(multiplexer_11_out), .b(2'b01), .gt(comparator_32_gt));  // open: eq, lt
  Multiplexer #(.width(32), .disabled(0)) multiplexer_17 (
    .in0(nPC_in), .in1(multiplexer_16_out), .out(multiplexer_17_out), .sel(comparator_32_gt), .en(hit));
  Multiplexer #(.select(2), .width(32), .disabled(0)) multiplexer_18 (
    .in0(a0), .in1(a1), .in2(a2), .in3(a3), .out(multiplexer_18_out), .sel(pos), .en(find));
  // Probe on will_go
  Multiplexer #(.select(2), .disabled(0)) multiplexer_19 (
    .in0(miss0), .in1(miss1), .in2(miss2), .in3(miss3), .out(multiplexer_19_out), .sel(pos), .en(find));
  Multiplexer #(.width(32), .disabled(0), .enable("false")) multiplexer_20 (
    .in0(nPC_in), .in1(multiplexer_17_out), .out(multiplexer_20_out), .sel(hit));
  Multiplexer #(.width(32), .disabled(0), .enable("false")) multiplexer_21 (
    .in0(new_entry), .in1(multiplexer_18_out), .out(multiplexer_21_out), .sel(if_success));
  and and_22 (and_22_out, if_j, if_success);
  Multiplexer #(.disabled(0), .enable("false")) multiplexer_22 (
    .in0(and_22_out), .in1(multiplexer_19_out), .out(miss), .sel(find));
  Multiplexer #(.width(32), .disabled(0), .enable("false")) multiplexer_23 (
    .in0(multiplexer_20_out), .in1(multiplexer_21_out), .out(npc), .sel(multiplexer_19_out));
endmodule
